# Fritzing sketch Circuit Diagram (saved by Fritzing 0.9.3b)
breadboards: 1

parts:
  U1 = ESP32-38PinWide [part_number=ESP32-38PinWide]
  S1 = H-Bridge with L298N
  M1 = DC Motor
  J1 = Basic Servo
  VCC1 = Battery block 9V

nets:
  N1: U1.GPIO12, S1.IN2
  N2: U1.GPIO13, S1.IN1
  GND: U1.GPIO11, S1.GND, J1.gnd, VCC1.-
  VIN: U1.VIN, S1.5V, J1.vcc
  N3: U1.GPIO5, J1.pulse
  N4: S1.12V, VCC1.+
  N5: S1.ENA, S1.ENA-5V
  N6: S1.M1-01, M1.pin_2
  N7: S1.M1-02, M1.pin_1

custom parts:
  ESP32-38PinWide: Generic 38-Pin ESP32 with wide format (only access to one side of pins on a breadboard) based on Stephen Lilley's HiLetgo ESP-WROOM-32 ESP32 ESP-32S Development Board.
  H-Bridge with L298N: h-bridge
